// Logisim project HalfAdd.circ as structural Verilog: 1 circuit, main circuit main
module main (
  input  x,
  input  y,
  output s,
  output c
);

  wire not_1_out, or_1_out;

  or or_1 (or_1_out, x, y);
  and and_1 (c, x, y);
  not not_1 (not_1_out, c);
  and and_2 (s, or_1_out, not_1_out);

  // Notes on the sheet:
  //   x + y
  //   xy
  //   Bộ nửa cộng (cộng 2 bit): Đầu vào 2 bit x,y, đầu ra là 2 bit s,c. Bit s là tổng, c là nhớ.
  //   Tổng = (x+y)((-x)(-y))
  //   Số nhớ = xy
endmodule
