// Logisim project testVector.circ as structural Verilog: 1 circuit, main circuit main
module main (
  input  Sel,
  input  IN1,
  input  IN2,
  output Out1
);

  wire and_1_out, and_2_out, not_1_out, not_2_out;

  not not_1 (not_1_out, Sel);
  not not_2 (not_2_out, not_1_out);
  and and_1 (and_1_out, not_2_out, IN1);
  and and_2 (and_2_out, not_1_out, IN2);
  or or_1 (Out1, and_1_out, and_2_out);
endmodule
